# Fritzing sketch Security (saved by Fritzing 0.9.3b)
breadboards: 1

parts:
  Raspberry_Pi_1 = Raspberry Pi 3 [part_number=RPI-3-V1.2]
  LED1 = RGB LED (com. cathode, rgb) [package="5 mm [THT]"]
  S1 = Pushbutton [package="[THT]"]
  J1 = Piezo Speaker
  R1 = Resistor [tolerance=±5% resistance=330 package=THT]
  R2 = Resistor [tolerance=±5% resistance=330 package=THT]
  R3 = Resistor [tolerance=±5% resistance=330 package=THT]
  S2 = Reed switch [package=THT]

nets:
  N1: Raspberry_Pi_1.GPIO3, J1.pin2
  N2: Raspberry_Pi_1.GIPO27, S2.pin_1
  N3: Raspberry_Pi_1.GIPO13, R2.Pin_1
  N4: Raspberry_Pi_1.GIPO19, R3.Pin_1
  N5: Raspberry_Pi_1.GIPO26, R1.Pin_1
  N6: Raspberry_Pi_1.GIPO21, S1.Pin_3, S1.Pin_4
  N7: LED1.red_anode, R2.Pin_0
  N8: LED1.common_cathode, R3.Pin_0
  N9: LED1.green_anode, S1.Pin_1, S1.Pin_2, J1.pin1, S2.pin_2
  N10: LED1.blue_anode, R1.Pin_0

notes:
  PIR motion sensor
  -vcc
  -out
  -gnd
  Raspberry Pi 4 Model B
  (c)Raspberry Pi 2018
  Buzzer
  RGB
  led
  Raspberry Pi NOIR camera
